// Logisim project CS23I1005-7down.circ as structural Verilog
module sevenandfour (
  input  in_1,
  input  in_2,
  input  in_3,
  input  in_4,
  input  in_5,
  input  in_6,
  input  in_7,
  input  in_8
);

  wire and_1_out, and_2_out, and_3_out, and_4_out, and_5_out, and_6_out, and_7_out, clock_1_out, not_1_out,
       not_2_out, not_3_out, or_1_out, t_ff_1_qn, t_ff_2_qn;
  wire [2:0] t_ff_1_q;
  wire [3:0] j_k_ff_1_q;

  not not_1 (not_1_out, in_1);
  Clock clock_1 (.out(clock_1_out));
  and and_1 (and_1_out, not_1_out, clock_1_out);
  J_K_Flip_Flop j_k_ff_1 (.J(or_1_out), .K(or_1_out), .clk(and_1_out), .Q(j_k_ff_1_q[0]));  // open: Qn, preset, reset
  T_Flip_Flop t_ff_1 (.T(in_6), .clk(and_1_out), .Q(t_ff_1_q[0]), .Qn(t_ff_1_qn), .reset(in_8), .preset(in_3));
  and and_2 (and_2_out, j_k_ff_1_q[0], or_1_out);
  J_K_Flip_Flop j_k_ff_2 (.J(and_2_out), .K(and_2_out), .clk(and_1_out), .Q(j_k_ff_1_q[1]));  // open: Qn, preset, reset
  T_Flip_Flop t_ff_2 (.T(t_ff_1_qn), .clk(and_1_out), .Q(t_ff_1_q[1]), .Qn(t_ff_2_qn), .reset(in_7), .preset(in_4));
  or or_1 (or_1_out, and_5_out, and_7_out);
  and and_3 (and_3_out, j_k_ff_1_q[1], and_2_out);
  and and_4 (and_4_out, t_ff_2_qn, t_ff_1_qn);
  J_K_Flip_Flop j_k_ff_3 (.J(and_3_out), .K(and_3_out), .clk(and_1_out), .Q(j_k_ff_1_q[2]));  // open: Qn, preset, reset
  T_Flip_Flop t_ff_3 (.T(and_4_out), .clk(and_1_out), .Q(t_ff_1_q[2]), .preset(in_2));  // open: Qn, reset
  and and_5 (and_5_out, t_ff_1_q[2], not_2_out, not_3_out);
  not not_2 (not_2_out, t_ff_1_q[1]);
  not not_3 (not_3_out, t_ff_1_q[0]);
  and and_6 (and_6_out, j_k_ff_1_q[2], and_3_out);
  Hex_Digit_Display hex_digit_display_1 (.value({in_5, t_ff_1_q}));  // open: dp
  J_K_Flip_Flop j_k_ff_4 (.J(and_6_out), .K(and_6_out), .clk(and_1_out), .Q(j_k_ff_1_q[3]));  // open: Qn, preset, reset
  and and_7 (and_7_out, t_ff_1_q[2], t_ff_1_q[1], t_ff_1_q[0]);
  Hex_Digit_Display hex_digit_display_2 (.value(j_k_ff_1_q));  // open: dp

  // Notes on the sheet:
  //   in_6: initial=0x1
  //   Stop Switch
endmodule

module fivecount (
  input  in_1,
  input  in_2,
  input  in_3,
  input  in_4,
  input  in_5,
  input  in_6,
  input  in_7,
  input  in_8
);

  wire and_1_out, and_2_out, and_3_out, and_4_out, and_5_out, and_6_out, and_7_out, clock_1_out, not_1_out,
       not_2_out, t_ff_1_qn, t_ff_2_qn;
  wire [2:0] t_ff_1_q;
  wire [3:0] j_k_ff_1_q;

  Clock clock_1 (.out(clock_1_out));
  and and_1 (and_1_out, clock_1_out, not_1_out);
  not not_1 (not_1_out, in_8);
  J_K_Flip_Flop j_k_ff_1 (.J(and_5_out), .K(and_5_out), .clk(and_1_out), .Q(j_k_ff_1_q[0]));  // open: Qn, preset, reset
  T_Flip_Flop t_ff_1 (.T(in_5), .clk(and_1_out), .Q(t_ff_1_q[0]), .Qn(t_ff_1_qn), .reset(in_7), .preset(in_2));
  and and_2 (and_2_out, j_k_ff_1_q[0], and_5_out);
  T_Flip_Flop t_ff_2 (.T(t_ff_1_qn), .clk(and_1_out), .Q(t_ff_1_q[1]), .Qn(t_ff_2_qn), .reset(in_6), .preset(in_3));
  J_K_Flip_Flop j_k_ff_2 (.J(and_2_out), .K(and_2_out), .clk(and_1_out), .Q(j_k_ff_1_q[1]));  // open: Qn, preset, reset
  and and_3 (and_3_out, t_ff_2_qn, t_ff_1_qn);
  and and_4 (and_4_out, j_k_ff_1_q[1], and_2_out);
  T_Flip_Flop t_ff_3 (.T(and_3_out), .clk(and_1_out), .Q(t_ff_1_q[2]), .preset(in_1));  // open: Qn, reset
  J_K_Flip_Flop j_k_ff_3 (.J(and_4_out), .K(and_4_out), .clk(and_1_out), .Q(j_k_ff_1_q[2]));  // open: Qn, preset, reset
  and and_5 (and_5_out, and_7_out, in_5);
  and and_6 (and_6_out, j_k_ff_1_q[2], and_4_out);
  not not_2 (not_2_out, t_ff_1_q[1]);
  J_K_Flip_Flop j_k_ff_4 (.J(and_6_out), .K(and_6_out), .clk(and_1_out), .Q(j_k_ff_1_q[3]));  // open: Qn, preset, reset
  Hex_Digit_Display hex_digit_display_1 (.value({in_4, t_ff_1_q}));  // open: dp
  and and_7 (and_7_out, t_ff_1_q[2], not_2_out, t_ff_1_q[0]);
  Hex_Digit_Display hex_digit_display_2 (.value(j_k_ff_1_q));  // open: dp

  // Notes on the sheet:
  //   in_5: initial=0x1
  //   Stop Switch
endmodule
